# Fritzing sketch Drone2 (saved by Fritzing 1.0.6)

parts:
  esp1 = ESP32 DevKitc V4
  Part1 = Thumb Joystick
  Part2 = Thumb Joystick
  Part3 = InvenSense MPU6050
  LCD2 = LCD screen
  L2 = Pushbutton [package="[THT]"]
  R1 = Pushbutton [package="[THT]"]
  R2 = Pushbutton [package="[THT]"]
  L1 = Pushbutton [package="[THT]"]
  Part4 = Triple Axis Magnetometer - HMC5883 Breakout
  U1 = PCF8574 [package="DIP16 [THT]"]
  Q2 = TRANSISTOR_NPN [package=to-92-ammo]
  R2_2 = Resistor [tolerance=±5% resistance=1k package="1206 [SMD]"]
  U7 = Vibration Motor- ROB-08449 [package=vibe-motor-10mm]
  NANOTX = female pin header, 8 pins [form="♀ (female)"]
  U4 = Battery Holders [package=lipo-1100mAh]
  Yükseltici = Mini-360 DC-DC Buck converter [package=THT]
  U8 = SWITCH-SPST-2 [package=switch-spst-vertical]
  SG1 = Buzzer 12mm [package=buzzer-ccv]
  U2 = SWITCH-SPST-2 [package=switch-spst-vertical]
  DÜŞÜRÜCÜ1 = Mini-360 DC-DC Buck converter [package=THT]
  R1_2 = Resistor [tolerance=±5% resistance=1k package="1206 [SMD]"]
  Q1 = TRANSISTOR_NPN [package=to-92-ammo]
  VCC1 = Battery block 9V [internal_resistance=0.1Ω]
  1N4007 = Rectifier Diode 400mil [part_number=1N4001 package="400 mil [THT]"]
  U9 = Vibration Motor- ROB-08449 [package=vibe-motor-10mm]
  1N4007_1 = Rectifier Diode 400mil [part_number=1N4001 package="400 mil [THT]"]
  LCM1602_IIC2 = LCM1602 IIC [part_number="LCM1602 IIC" chip_label="LCM1602 IIC" package="DIP (Dual Inline) [THT]"]
  Keypad4x2 = Keypad Membran 4x4
  2s_şarj = 2S-BMS
  TP1 = TP4056 [chip_label=TP4056 package="DIP (Dual Inline) [THT]"]
  Part5 = Adafruit Proto Shield for Arduino Kit - v.5  # not connected

nets:
  N1: esp1.IO15, R2_2.Pin_1
  N2: esp1.IO2, SG1.2
  N3: esp1.IO4, R1_2.Pin_0
  N4: esp1.IO17, NANOTX.pin1
  N5: esp1.IO18, L1.Pin_3, L1.Pin_4
  N6: esp1.IO19, L2.Pin_3, L2.Pin_4
  N7: esp1.IO21, Part3.SDA, Part4.GND, U1.A2, LCM1602_IIC2.SDA
  N8: esp1.IO22, Part3.SCL, Part4.VCC, U1.P0, LCM1602_IIC2.SCL
  GND: esp1.GND, Part1.GND, Part3.GND, L2.Pin_1, L2.Pin_2, R2.Pin_1, R2.Pin_2, Part4.SDA, U1.A1, Q2.C, NANOTX.pin2, U4.-, Yükseltici.IN-, Yükseltici.OUT-, SG1.1, DÜŞÜRÜCÜ1.IN-, DÜŞÜRÜCÜ1.OUT-, Q1.C, VCC1.-, LCM1602_IIC2.GND, 2s_şarj.pin2, 2s_şarj.pin3#2, TP1.pin2, TP1.pin5, TP1.pin6
  VCC: esp1.3V3, Part1.VCC, Part3.VCC, Part4.SCL, U1.A0, LCM1602_IIC2.VCC
  N9: esp1.IO34, Part2.HORZ
  N10: esp1.IO35, Part2.VERT
  N11: esp1.IO32, Part1.HORZ
  N12: esp1.IO33, Part1.VERT
  N13: esp1.IO25, Part1.SEL
  N14: esp1.IO26, Part2.SEL
  N15: esp1.IO27, R1.Pin_3, R1.Pin_4
  N16: esp1.IO14, R2.Pin_3, R2.Pin_4
  N17: esp1.5V, Yükseltici.OUT+
  VSS: LCD2.VSS, LCM1602_IIC2.VSS
  VDD: LCD2.VDD, LCM1602_IIC2.VDD
  N18: LCD2.V0, LCM1602_IIC2.V0
  N19: LCD2.RS, LCM1602_IIC2.RS
  N20: LCD2.R/W, LCM1602_IIC2.RW
  N21: LCD2.E, LCM1602_IIC2.E
  N22: LCD2.DB0, LCM1602_IIC2.D0
  N23: LCD2.DB1, LCM1602_IIC2.D1
  N24: LCD2.DB2, LCM1602_IIC2.D2
  N25: LCD2.DB3, LCM1602_IIC2.D3
  N26: LCD2.DB4, LCM1602_IIC2.D4
  N27: LCD2.DB5, LCM1602_IIC2.D5
  N28: LCD2.DB6, LCM1602_IIC2.D6
  N29: LCD2.DB7, LCM1602_IIC2.D7
  N30: LCD2.LED+, LCM1602_IIC2.A
  N31: LCD2.LED-, LCM1602_IIC2.K
  N32: U1.P4, Keypad4x2.Pin8
  N33: U1.P5, Keypad4x2.Pin7
  N34: U1.P6, Keypad4x2.Pin6
  N35: U1.P7, Keypad4x2.Pin5
  N36: U1.INT, Keypad4x2.Pin4
  N37: U1.SCL, Keypad4x2.Pin3
  N38: U1.SDA, Keypad4x2.Pin2
  N39: U1.VCC, Keypad4x2.Pin1
  N40: Q2.E, U9.+
  N41: Q2.B, R2_2.Pin_0
  N42: U7.+, Q1.E
  N43: U7.-, 1N4007.cathode
  N44: NANOTX.pin3, U2.O
  N45: U4.+, U8.P, TP1.pin4
  N46: Yükseltici.IN+, U8.O, TP1.pin1, TP1.pin3
  N47: U2.P, DÜŞÜRÜCÜ1.IN+, VCC1.+, 2s_şarj.pin1, 2s_şarj.pin3#3
  N48: DÜŞÜRÜCÜ1.OUT+, 1N4007.anode, 1N4007_1.anode
  N49: R1_2.Pin_1, Q1.B
  N50: U9.-, 1N4007_1.cathode
  N51: LCM1602_IIC2.LED_A, LCM1602_IIC2.LED_B

custom parts:
  ESP32 DevKitc V4: ESP32-DevKitC board with ESP32-WROOM-32 module. ESP32-DevKitC V4 is a small-sized ESP32-based development board produced by Espressif. Most of the pins on the ESP module are broken out to the pin headers on the board. The pins D0, D1, D2, D3, CMD and CLK are used internally for communication between ESP32 and SPI flash memory. They are grouped on both sides near the USB connector. Avoid using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
  Mini-360 DC-DC Buck converter: Mini-360 DC-DC Buck converter. Tiny buck step down voltage converter, input voltage 4.75 to 23V output 1 to 17V adjustable. Available from ebay and the like.
  Rectifier Diode 400mil: A standard rectifier diode streched to 400mil
  LCM1602 IIC: I2C-Module to use a 1602 or 2004 LCD on with the wire.h libory Serial LCD Modul
  Keypad Membran 4x4: Membrane Keypad 4x4 Matrix
  2S-BMS: 2S-BMS LIPO battery charger / protection unit. Note pcb does not match the board as it will likely connect with wires, so pcb is 5 pads suitable for .1in header pins.
  TP4056: A DIP stand-in part for whatever IC you want. With 6 pins on a 300mil dual inline package (DIP) footprint.
  Adafruit Proto Shield for Arduino Kit - v.5: Arduino prototyping shield designed by Adafruit Industries
