# Fritzing sketch caplemaping (saved by Fritzing 1.0.6)

parts:
  Part6 = Adafruit Proto Shield for Arduino Kit - v.5  # not connected
  1N4007_2 = Rectifier Diode 400mil [part_number=1N4001 package="400 mil [THT]"]
  1N4007_3 = Rectifier Diode 400mil [part_number=1N4001 package="400 mil [THT]"]
  2s_şarj1 = 2S-BMS
  TP2 = TP4056 [chip_label=TP4056 package="DIP (Dual Inline) [THT]"]
  LCM1602_IIC3 = LCM1602 IIC [part_number="LCM1602 IIC" chip_label="LCM1602 IIC" package="DIP (Dual Inline) [THT]"]
  Keypad4x3 = Keypad Membran 4x4
  Q3 = TRANSISTOR_NPN [package=to-92-ammo]
  Q4 = TRANSISTOR_NPN [package=to-92-ammo]
  R3 = Resistor [tolerance=±5% resistance=1k package="1206 [SMD]"]
  R4 = Resistor [tolerance=±5% resistance=1k package="1206 [SMD]"]
  U10 = SWITCH-SPST-2 [package=switch-spst-vertical]
  U11 = SWITCH-SPST-2 [package=switch-spst-vertical]
  U12 = Battery Holders [package=lipo-1100mAh]
  Yükseltici1 = Mini-360 DC-DC Buck converter [package=THT]
  DÜŞÜRÜCÜ2 = Mini-360 DC-DC Buck converter [package=THT]
  U13 = Vibration Motor- ROB-08449 [package=vibe-motor-10mm]
  U14 = Vibration Motor- ROB-08449 [package=vibe-motor-10mm]
  NANOTX1 = female pin header, 8 pins [form="♀ (female)"]
  VCC2 = Battery block 9V [internal_resistance=0.1Ω]
  SG2 = Buzzer 12mm [package=buzzer-ccv]
  LCD3 = LCD screen
  esp2 = ESP32 DevKitc V4
  Part7 = Thumb Joystick
  Part8 = Thumb Joystick
  Part9 = InvenSense MPU6050
  L3 = Pushbutton [package="[THT]"]
  R5 = Pushbutton [package="[THT]"]
  R6 = Pushbutton [package="[THT]"]
  L4 = Pushbutton [package="[THT]"]
  Part10 = Triple Axis Magnetometer - HMC5883 Breakout
  U15 = PCF8574 [package="DIP16 [THT]"]

nets:
  N1: 1N4007_2.cathode, U13.-
  N2: 1N4007_2.anode, 1N4007_3.anode, DÜŞÜRÜCÜ2.OUT+
  N3: 1N4007_3.cathode, U14.-
  N4: 2s_şarj1.pin1, 2s_şarj1.pin3#3, U11.P, DÜŞÜRÜCÜ2.IN+, VCC2.+
  GND: 2s_şarj1.pin2, 2s_şarj1.pin3#2, TP2.pin2, TP2.pin5, TP2.pin6, LCM1602_IIC3.GND, Q3.C, Q4.C, U12.-, Yükseltici1.IN-, Yükseltici1.OUT-, DÜŞÜRÜCÜ2.IN-, DÜŞÜRÜCÜ2.OUT-, NANOTX1.pin2, VCC2.-, SG2.1, esp2.GND, Part7.GND, Part9.GND, R5.Pin_1, R5.Pin_2, L4.Pin_1, L4.Pin_2, Part10.SDA, U15.A1
  N5: TP2.pin1, TP2.pin3, U10.O, Yükseltici1.IN+
  N6: TP2.pin4, U10.P, U12.+
  VSS: LCM1602_IIC3.VSS, LCD3.VSS
  VDD: LCM1602_IIC3.VDD, LCD3.VDD
  N7: LCM1602_IIC3.V0, LCD3.V0
  N8: LCM1602_IIC3.RS, LCD3.RS
  N9: LCM1602_IIC3.RW, LCD3.R/W
  N10: LCM1602_IIC3.E, LCD3.E
  N11: LCM1602_IIC3.D0, LCD3.DB0
  N12: LCM1602_IIC3.D1, LCD3.DB1
  N13: LCM1602_IIC3.D2, LCD3.DB2
  N14: LCM1602_IIC3.D3, LCD3.DB3
  N15: LCM1602_IIC3.D4, LCD3.DB4
  N16: LCM1602_IIC3.D5, LCD3.DB5
  N17: LCM1602_IIC3.D6, LCD3.DB6
  N18: LCM1602_IIC3.D7, LCD3.DB7
  N19: LCM1602_IIC3.A, LCD3.LED+
  N20: LCM1602_IIC3.K, LCD3.LED-
  VCC: LCM1602_IIC3.VCC, esp2.3V3, Part7.VCC, Part9.VCC, Part10.SCL, U15.A0
  N21: LCM1602_IIC3.SDA, esp2.IO21, Part9.SDA, Part10.GND, U15.A2
  N22: LCM1602_IIC3.SCL, esp2.IO22, Part9.SCL, Part10.VCC, U15.P0
  N23: LCM1602_IIC3.LED_A, LCM1602_IIC3.LED_B
  N24: Keypad4x3.Pin1, U15.VCC
  N25: Keypad4x3.Pin2, U15.SDA
  N26: Keypad4x3.Pin3, U15.SCL
  N27: Keypad4x3.Pin4, U15.INT
  N28: Keypad4x3.Pin5, U15.P7
  N29: Keypad4x3.Pin6, U15.P6
  N30: Keypad4x3.Pin7, U15.P5
  N31: Keypad4x3.Pin8, U15.P4
  N32: Q3.E, U13.+
  N33: Q3.B, R3.Pin_0
  N34: Q4.E, U14.+
  N35: Q4.B, R4.Pin_1
  N36: R3.Pin_1, esp2.IO15
  N37: R4.Pin_0, esp2.IO4
  N38: U11.O, NANOTX1.pin3
  N39: Yükseltici1.OUT+, esp2.5V
  N40: NANOTX1.pin1, esp2.IO17
  N41: SG2.2, esp2.IO2
  N42: esp2.IO18, L3.Pin_3, L3.Pin_4
  N43: esp2.IO19, L4.Pin_3, L4.Pin_4
  N44: esp2.IO34, Part8.HORZ
  N45: esp2.IO35, Part8.VERT
  N46: esp2.IO32, Part7.HORZ
  N47: esp2.IO33, Part7.VERT
  N48: esp2.IO25, Part7.SEL
  N49: esp2.IO26, Part8.SEL
  N50: esp2.IO27, R6.Pin_3, R6.Pin_4
  N51: esp2.IO14, R5.Pin_3, R5.Pin_4

custom parts:
  Adafruit Proto Shield for Arduino Kit - v.5: Arduino prototyping shield designed by Adafruit Industries
  Rectifier Diode 400mil: A standard rectifier diode streched to 400mil
  2S-BMS: 2S-BMS LIPO battery charger / protection unit. Note pcb does not match the board as it will likely connect with wires, so pcb is 5 pads suitable for .1in header pins.
  TP4056: A DIP stand-in part for whatever IC you want. With 6 pins on a 300mil dual inline package (DIP) footprint.
  LCM1602 IIC: I2C-Module to use a 1602 or 2004 LCD on with the wire.h libory Serial LCD Modul
  Keypad Membran 4x4: Membrane Keypad 4x4 Matrix
  Mini-360 DC-DC Buck converter: Mini-360 DC-DC Buck converter. Tiny buck step down voltage converter, input voltage 4.75 to 23V output 1 to 17V adjustable. Available from ebay and the like.
  ESP32 DevKitc V4: ESP32-DevKitC board with ESP32-WROOM-32 module. ESP32-DevKitC V4 is a small-sized ESP32-based development board produced by Espressif. Most of the pins on the ESP module are broken out to the pin headers on the board. The pins D0, D1, D2, D3, CMD and CLK are used internally for communication between ESP32 and SPI flash memory. They are grouped on both sides near the USB connector. Avoid using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
