# Fritzing sketch untitled_sketch2 (saved by Fritzing 1.0.6)

parts:
  Part16 = Adafruit Proto Shield for Arduino Kit - v.5
  1N4007_6 = Rectifier Diode 400mil [part_number=1N4001 package="400 mil [THT]"]
  1N4007_7 = Rectifier Diode 400mil [part_number=1N4001 package="400 mil [THT]"]  # not connected
  2s_şarj3 = 2S-BMS
  TP4 = TP4056 [chip_label=TP4056 package="DIP (Dual Inline) [THT]"]
  Q7 = TRANSISTOR_NPN [package=to-92-ammo]
  Q8 = TRANSISTOR_NPN [package=to-92-ammo]
  R11 = Resistor [tolerance=±5% resistance=1k package="1206 [SMD]"]
  R12 = Resistor [tolerance=±5% resistance=1k package="1206 [SMD]"]
  U22 = SWITCH-SPST-2 [package=switch-spst-vertical]
  U23 = SWITCH-SPST-2 [package=switch-spst-vertical]
  U24 = Battery Holders [package=lipo-1100mAh]
  Yükseltici3 = Mini-360 DC-DC Buck converter [package=THT]
  DÜŞÜRÜCÜ4 = Mini-360 DC-DC Buck converter [package=THT]
  U25 = Vibration Motor- ROB-08449 [package=vibe-motor-10mm]
  U26 = Vibration Motor- ROB-08449 [package=vibe-motor-10mm]
  NANOTX3 = female pin header, 8 pins [form="♀ (female)"]
  VCC4 = Battery block 9V [internal_resistance=0.1Ω]
  SG4 = Buzzer 12mm [package=buzzer-ccv]
  esp4 = ESP32 DevKitc V4
  Part17 = Thumb Joystick
  Part18 = Thumb Joystick
  Part19 = InvenSense MPU6050
  L7 = Pushbutton [package="[THT]"]
  R13 = Pushbutton [package="[THT]"]
  R14 = Pushbutton [package="[THT]"]
  L8 = Pushbutton [package="[THT]"]
  Part20 = Triple Axis Magnetometer - HMC5883 Breakout

nets:
  GND: Part16.GND, Part16.P$2#17, Part16.P$5#20, Part16.P$6, Part16.P$7, Part16.P$8, Part16.P$9, Part16.P$10, Part16.P$11, Part16.P$12, Yükseltici3.OUT-, DÜŞÜRÜCÜ4.IN-, DÜŞÜRÜCÜ4.OUT-, NANOTX3.pin2, VCC4.-, SG4.1, esp4.GND, Part17.GND, Part19.GND, L8.Pin_1, L8.Pin_2, Part20.SDA
  VCC: Part16.+5V, Part16.P$2#216, Part16.P$3, Part16.P$4, Part16.P$5#219, Yükseltici3.OUT+, esp4.5V, Part17.VCC, Part19.VCC, Part20.SCL
  N1: Part16.N$111, esp4.IO22
  N2: Part16.N$134, esp4.IO21
  N3: Part16.N$141, Part19.SCL
  N4: Part16.N$144, Part19.SDA
  N5: Part16.N$160, Part20.VCC
  N6: Part16.N$163, Part20.GND
  N7: 1N4007_6.cathode, DÜŞÜRÜCÜ4.OUT+, U25.-
  N8: 2s_şarj3.pin1, U23.P, DÜŞÜRÜCÜ4.IN+, VCC4.+
  N9: TP4.pin3, U22.P
  N10: TP4.pin4, U24.+
  N11: TP4.pin5, U24.-
  N12: TP4.pin6, Yükseltici3.IN-
  N13: Q7.B, R11.Pin_0
  N14: Q7.C, U25.+
  N15: Q8.B, R12.Pin_1
  N16: Q8.C, U26.+
  N17: R11.Pin_1, esp4.IO15
  N18: R12.Pin_0, esp4.IO4
  N19: U22.O, Yükseltici3.IN+
  N20: U23.O, NANOTX3.pin3
  N21: NANOTX3.pin1, esp4.IO17
  N22: SG4.2, esp4.IO2
  N23: esp4.IO18, L7.Pin_3, L7.Pin_4
  N24: esp4.IO19, L8.Pin_3, L8.Pin_4
  N25: esp4.IO34, Part18.HORZ
  N26: esp4.IO35, Part18.VERT
  N27: esp4.IO32, Part17.HORZ
  N28: esp4.IO33, Part17.VERT
  N29: esp4.IO25, Part17.SEL
  N30: esp4.IO26, Part18.SEL
  N31: esp4.IO27, R14.Pin_3, R14.Pin_4
  N32: esp4.IO14, R13.Pin_3, R13.Pin_4
  N33: L7.Pin_1, L7.Pin_2, R13.Pin_1, R13.Pin_2, R14.Pin_1, R14.Pin_2

custom parts:
  Adafruit Proto Shield for Arduino Kit - v.5: Arduino prototyping shield designed by Adafruit Industries
  Rectifier Diode 400mil: A standard rectifier diode streched to 400mil
  2S-BMS: 2S-BMS LIPO battery charger / protection unit. Note pcb does not match the board as it will likely connect with wires, so pcb is 5 pads suitable for .1in header pins.
  TP4056: A DIP stand-in part for whatever IC you want. With 6 pins on a 300mil dual inline package (DIP) footprint.
  Mini-360 DC-DC Buck converter: Mini-360 DC-DC Buck converter. Tiny buck step down voltage converter, input voltage 4.75 to 23V output 1 to 17V adjustable. Available from ebay and the like.
  ESP32 DevKitc V4: ESP32-DevKitC board with ESP32-WROOM-32 module. ESP32-DevKitC V4 is a small-sized ESP32-based development board produced by Espressif. Most of the pins on the ESP module are broken out to the pin headers on the board. The pins D0, D1, D2, D3, CMD and CLK are used internally for communication between ESP32 and SPI flash memory. They are grouped on both sides near the USB connector. Avoid using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
